// Logisim project Four_Bits_Add_Sub.circ as structural Verilog: 2 circuits, main circuit Add_Sub_4Bits
module Add_Sub_4Bits (
  input  [3:0] A,
  input  [3:0] B,
  input  Add_Sub,
  output [3:0] R,
  output Zero,
  output Overflow
);

  wire add_1bit_1_cout, add_1bit_2_cout, add_1bit_3_cout;

  // Probe on A
  // Probe on B
  Add_1Bit add_1bit_1 (.Cout(add_1bit_1_cout), .B(A[0]), .A(B[0]));  // open: Sum, Cin
  Add_1Bit add_1bit_2 (.Cout(add_1bit_2_cout), .B(A[1]), .A(B[1]), .Cin(add_1bit_1_cout));  // open: Sum
  Add_1Bit add_1bit_3 (.Cout(add_1bit_3_cout), .B(A[2]), .A(B[2]), .Cin(add_1bit_2_cout));  // open: Sum
  Add_1Bit add_1bit_4 (.B(A[3]), .A(B[3]), .Cin(add_1bit_3_cout));  // open: Cout, Sum
  // Probe on R

  // Notes on the sheet:
  //   Simon Zheng 260744353
  //   MAKE SURE THAT YOU OPENED THIS PROJECT IN "LOGISIM-EVOLUTION"
  //   YOU CAN FIND "LOGISIM-EVOLUTION" PROGRAM IN THE ASSIGNMENT'S FOLDER
  //   DO NOT USE "LOGISIM" VERSION TO SOLVE THIS ASSIGNMENT!
endmodule

module Add_1Bit (
  input  Cin,
  input  A,
  input  B,
  output Sum,
  output Cout
);

  wire and_1_out, and_2_out, xor_1_out;

  xor xor_1 (xor_1_out, A, B);
  and and_1 (and_1_out, xor_1_out, Cin);
  and and_2 (and_2_out, A, B);
  xor xor_2 (Sum, Cin, xor_1_out);
  or or_1 (Cout, and_1_out, and_2_out);

  // Notes on the sheet:
  //   Simon Zheng 260744353
  //   MAKE SURE THAT YOU OPENED THIS PROJECT IN "LOGISIM-EVOLUTION"
  //   YOU CAN FIND "LOGISIM-EVOLUTION" PROGRAM IN THE ASSIGNMENT'S FOLDER
  //   DO NOT USE "LOGISIM" VERSION TO SOLVE THIS ASSIGNMENT!
endmodule
